# Fritzing sketch watch_circuit_diagram (saved by Fritzing 0.9.3b)

parts:
  LCD1 = 2.8" SPI TFT Module [part_number="2.4ich TFT"]
  s1 = MAX30102
  s2 = Adafruit ADXL345 [part_number=ADXL345]
  R1 = Resistor [tolerance=±5% resistance=4.7k package=THT]
  R2 = Resistor [tolerance=±5% resistance=4.7k package=THT]
  U2 = Tiny RTC
  U1 = LuaNode32 / ESP32 [part_number=ESP32]

nets:
  VIN: LCD1.pin1, LCD1.pin8, s1.VIN, s2.3.3V, U2.VCC, U1.3V3
  GND: LCD1.pin2, s1.GND, s2.GND, U2.GND, U1.GND
  N1: LCD1.pin3, U1.D15
  N2: LCD1.pin4, U1.D4
  N3: LCD1.pin5, U1.D2
  N4: LCD1.pin6, LCD1.pin12, LCD1.pin17, U1.D23
  N5: LCD1.pin7, LCD1.pin10, LCD1.pin15, U1.D18
  N6: LCD1.pin9, LCD1.pin13, LCD1.pin16, U1.D19
  N7: LCD1.pin11, U1.D13
  N8: LCD1.pin14, U1.D26
  N9: LCD1.pin18, U1.D5
  N10: s1.SCL, s2.SCL, R1.Pin_0, U2.SCL, U1.D22
  N11: s1.SDA, s2.SDA/SDIO, R2.Pin_0, U2.SDA, U1.D21
  N12: R1.Pin_1, R2.Pin_1

custom parts:
  2.8" SPI TFT Module: A generic 2.8 inch LCD TFT 320x240 display with touchscreen and SD card slot. Uses the ILI9341 controller, like the Adafruit displays of this size uses.
  MAX30102: Oximeter module using the MAX30102 chip. You may wish to read (and check your module) this post on power problems with these modules: https://reedpaper.wordpress.com/2018/08/22/pulse-oximeter-max30100-max30102-how-to-fix-wrong-board/ . As usual, if you want the mounting holes in pcb, you need to drag a hole over the pad in silkscreen to actually drill the hole (by default they are not drilled)
  Adafruit ADXL345: Filling out our accelerometer offerings, we now have the really lovely digital ADXL345 from Analog Devices, a triple-axis accelerometer with digital I2C and SPI interface breakout. We added an on-board 3.3V regulator and logic-level shifting circuitry, making it a perfect choice for interfacing with any 3V or 5V microcontroller such as the Arduino. The sensor has three axes of measurements, X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
  Tiny RTC: Tiny RTC I2C module DS1370Z RTC and AT24C32 EEPROM
  LuaNode32 / ESP32: New Image for LuaNode32 DOIT ESP32 DEVKIT V1. Base parts from LuaNode32 / ESP32 ESP32 based LuaNode32 by G.Noorlander DOIT Esp32 DevKit v1 (30 pins long, 11 pins width) by Werner Rothschopf (modified by vanepp Dec 2018)
